# Fritzing sketch ledbutton (saved by Fritzing 1.0.3b)
breadboards: 1

parts:
  MH-ET_LIVE_ESP32_DEVKIT1 = MH-ET LIVE ESP32 DEVKIT 38 pins
  LED1 = smd LED [color="Red (633nm)" package="0805 [SMD]"]
  R1 = Resistor [tolerance=±5% resistance=220 package="0402 [SMD]"]
  R2 = Resistor [tolerance=±5% resistance=220 package="0402 [SMD]"]
  S2 = SWITCH-MOMENTARY-2 [package=tactile_switch_smd-2]

nets:
  N1: MH-ET_LIVE_ESP32_DEVKIT1.3V3, S2.1
  N2: MH-ET_LIVE_ESP32_DEVKIT1.IO32, R1.Pin_1
  N3: MH-ET_LIVE_ESP32_DEVKIT1.IO33, R2.Pin_1, S2.2
  N4: MH-ET_LIVE_ESP32_DEVKIT1.GND#58, LED1.cathode, R2.Pin_0
  N5: LED1.anode, R1.Pin_0

custom parts:
  MH-ET LIVE ESP32 DEVKIT 38 pins: http://mh.nodebb.com/topic/2/mh-et-live-esp32-devkit
