# Fritzing sketch fade_led_poti (saved by Fritzing 1.0.3b)
breadboards: 1

parts:
  LED1 = smd LED [color="Red (633nm)" package="0805 [SMD]"]
  MH-ET_LIVE_ESP32_DEVKIT1 = MH-ET LIVE ESP32 DEVKIT 38 pins
  R1 = Resistor [tolerance=±5% resistance=220 package="2010 [SMD]"]
  R2 = 6mm Trimmer Potentiometer [maximum_resistance=10kΩ knob_status=50% power=0.5W package=THT]

nets:
  N1: LED1.cathode, R1.Pin_1
  N2: LED1.anode, MH-ET_LIVE_ESP32_DEVKIT1.IO32
  N3: MH-ET_LIVE_ESP32_DEVKIT1.3V3, R2.leg2
  N4: MH-ET_LIVE_ESP32_DEVKIT1.IO33, R2.wiper
  N5: MH-ET_LIVE_ESP32_DEVKIT1.GND#58, R1.Pin_0, R2.leg1

custom parts:
  MH-ET LIVE ESP32 DEVKIT 38 pins: http://mh.nodebb.com/topic/2/mh-et-live-esp32-devkit
