# Fritzing sketch dht11-display (saved by Fritzing 1.0.3b)
breadboards: 1

parts:
  MH-ET_LIVE_ESP32_DEVKIT1 = MH-ET LIVE ESP32 DEVKIT 38 pins
  LCM1602_IIC1 = LCM1602 IIC [part_number="LCM1602 IIC" chip_label="LCM1602 IIC" package="DIP (Dual Inline) [THT]"]
  U1 = LCD-16X2 [package=lcd-8x2-kit]  # not connected
  DHT1 = Humidity and Temperature Sensor DHT11

nets:
  3V3: MH-ET_LIVE_ESP32_DEVKIT1.3V3, DHT1.Vcc
  N1: MH-ET_LIVE_ESP32_DEVKIT1.IO14, DHT1.Data-signal
  N2: MH-ET_LIVE_ESP32_DEVKIT1.GND#58, LCM1602_IIC1.GND, DHT1.GND_2
  5V: MH-ET_LIVE_ESP32_DEVKIT1.5V, LCM1602_IIC1.VCC
  N3: MH-ET_LIVE_ESP32_DEVKIT1.IO22, LCM1602_IIC1.SCL
  N4: MH-ET_LIVE_ESP32_DEVKIT1.IO21, LCM1602_IIC1.SDA

custom parts:
  MH-ET LIVE ESP32 DEVKIT 38 pins: http://mh.nodebb.com/topic/2/mh-et-live-esp32-devkit
  LCM1602 IIC: I2C-Module to use a 1602 or 2004 LCD on with the wire.h libory Serial LCD Modul
  Humidity and Temperature Sensor DHT11: Digital relative humidity & temperature sensor DHT11
